// Logisim project 实验5-CS200X-0618-Yuigahama.circ as structural Verilog
module \四位二进制可逆计数器  (
  input  CPD,
  input  CPU,
  input  A,
  input  B,
  input  C,
  input  D,
  input  nLD,
  input  CLR,
  output QA,
  output QB,
  output QC,
  output QD
);

  wire and_1_out, and_2_out, and_3_out, and_4_out, and_5_out, and_6_out, and_7_out, and_8_out, and_9_out,
       and_10_out, and_11_out, and_12_out, and_13_out, and_14_out, d_ff_1_qn, d_ff_2_qn, d_ff_3_qn,
       d_ff_4_qn, not_1_out, not_2_out, not_3_out, not_4_out, not_5_out, or_1_out, or_2_out, or_3_out,
       or_4_out, or_5_out, or_6_out, or_7_out, or_8_out;

  and and_1 (and_1_out, d_ff_1_qn, CPD);
  and and_2 (and_2_out, QA, CPU);
  and and_3 (and_3_out, d_ff_1_qn, d_ff_2_qn, CPD);
  and and_4 (and_4_out, QA, QB, CPU);
  and and_5 (and_5_out, d_ff_1_qn, d_ff_2_qn, d_ff_3_qn, CPD);
  and and_6 (and_6_out, QA, QB, QC, CPU);
  or or_1 (or_1_out, CPD, CPU);
  or or_2 (or_2_out, and_1_out, and_2_out);
  or or_3 (or_3_out, and_3_out, and_4_out);
  or or_4 (or_4_out, and_5_out, and_6_out);
  D_Flip_Flop #(.trigger("falling"), .Pre_Clr_Positions("LEGACY"), .NegatePresetClear("false"), .enable("true"), .NewFFLayout("false")) d_ff_1 (
    .clk(or_1_out), .D(d_ff_1_qn), .Q(QA), .Qn(d_ff_1_qn), .preset(and_7_out), .en(nLD), .reset(or_5_out));
  D_Flip_Flop #(.trigger("falling"), .Pre_Clr_Positions("LEGACY"), .NegatePresetClear("false"), .enable("true"), .NewFFLayout("false")) d_ff_2 (
    .clk(or_2_out), .D(d_ff_2_qn), .Q(QB), .Qn(d_ff_2_qn), .preset(and_9_out), .en(nLD), .reset(or_6_out));
  D_Flip_Flop #(.trigger("falling"), .Pre_Clr_Positions("LEGACY"), .NegatePresetClear("false"), .enable("true"), .NewFFLayout("false")) d_ff_3 (
    .clk(or_3_out), .D(d_ff_3_qn), .Q(QC), .Qn(d_ff_3_qn), .preset(and_11_out), .en(nLD), .reset(or_7_out));
  D_Flip_Flop #(.trigger("falling"), .Pre_Clr_Positions("LEGACY"), .NegatePresetClear("false"), .enable("true"), .NewFFLayout("false")) d_ff_4 (
    .clk(or_4_out), .D(d_ff_4_qn), .Q(QD), .Qn(d_ff_4_qn), .preset(and_13_out), .en(nLD), .reset(or_8_out));
  or or_5 (or_5_out, CLR, and_8_out);
  or or_6 (or_6_out, CLR, and_10_out);
  or or_7 (or_7_out, CLR, and_12_out);
  or or_8 (or_8_out, CLR, and_14_out);
  and and_7 (and_7_out, not_1_out, A);
  and and_8 (and_8_out, not_1_out, not_2_out);
  and and_9 (and_9_out, not_1_out, B);
  and and_10 (and_10_out, not_1_out, not_3_out);
  and and_11 (and_11_out, not_1_out, C);
  and and_12 (and_12_out, not_1_out, not_4_out);
  and and_13 (and_13_out, not_1_out, D);
  and and_14 (and_14_out, not_1_out, not_5_out);
  not not_1 (not_1_out, nLD);
  not not_2 (not_2_out, A);
  not not_3 (not_3_out, B);
  not not_4 (not_4_out, C);
  not not_5 (not_5_out, D);
endmodule

module \六十进制计数器  (
  input  CPU,
  input  CPD,
  input  Adj,
  input  Clr,
  output Q0d,
  output Q1d,
  output Q0c,
  output Q1c,
  output Q0b,
  output nQcc,
  output Q1b,
  output Q0a,
  output Q1a
);

  wire and_1_out, and_2_out, and_3_out, and_4_out, and_6_out, not_1_out, not_2_out, not_3_out, not_4_out,
       or_1_out, or_2_out, or_3_out, or_4_out;

  and and_1 (and_1_out, CPD, Adj);
  or or_1 (or_1_out, Q0a, Q0b, or_3_out, Q0c, Q0d);
  and and_2 (and_2_out, or_1_out, and_1_out);
  or or_2 (or_2_out, and_4_out, Clr);
  not not_1 (not_1_out, Q0a);
  not not_2 (not_2_out, Q0c);
  \四位二进制可逆计数器  \u_四位二进制可逆计数器_1  (
    .CPD(and_2_out), .CPU(CPU), .QA(Q0a), .A(1'b1), .QB(Q0b), .B(1'b0), .QC(Q0c), .C(1'b0), .QD(Q0d),
    .D(1'b1), .nLD(not_3_out), .CLR(or_2_out));
  and and_3 (and_3_out, Q0a, Q0b, Q0c, Q0d);
  and and_4 (and_4_out, not_1_out, Q0b, not_2_out, Q0d);
  not not_3 (not_3_out, and_3_out);
  and and_5 (nQcc, not_4_out, and_6_out);
  not not_4 (not_4_out, Adj);
  or or_3 (or_3_out, Q1a, Q1b, Q1c, Q1d);
  and and_6 (and_6_out, Q1b, Q1c);
  or or_4 (or_4_out, and_6_out, Clr);
  \四位二进制可逆计数器  \u_四位二进制可逆计数器_2  (
    .CPD(and_3_out), .CPU(and_4_out), .QA(Q1a), .A(1'b0), .QB(Q1b), .B(1'b0), .QC(Q1c), .C(1'b0), .QD(Q1d),
    .D(1'b0), .nLD(1'b1), .CLR(or_4_out));
endmodule

module \六十进制计数器测试电路  (
  input  in_1,
  input  in_2,
  input  in_3,
  input  in_4
);

  wire button_1_out, button_2_out, button_3_out, \六十进制计数器_1_nqcc ;
  wire [3:0] \六十进制计数器_1_q0a , \六十进制计数器_1_q1a , \六十进制计数器_2_q0a , \六十进制计数器_2_q1a ;

  Button button_1 (.out(button_1_out));
  Button button_2 (.out(button_2_out));
  \六十进制计数器  \u_六十进制计数器_1  (
    .Adj(in_1), .Q0d(\六十进制计数器_1_q0a [3]), .Q0c(\六十进制计数器_1_q0a [2]), .Q0b(\六十进制计数器_1_q0a [1]),
    .Q0a(\六十进制计数器_1_q0a [0]), .nQcc(\六十进制计数器_1_nqcc ), .Q1d(\六十进制计数器_1_q1a [3]), .Q1c(\六十进制计数器_1_q1a [2]),
    .Q1b(\六十进制计数器_1_q1a [1]), .Q1a(\六十进制计数器_1_q1a [0]), .Clr(in_3), .CPU(button_1_out), .CPD(button_2_out));
  Hex_Digit_Display hex_digit_display_1 (.value(\六十进制计数器_1_q1a ));  // open: dp
  Hex_Digit_Display hex_digit_display_2 (.value(\六十进制计数器_1_q0a ));  // open: dp
  Button button_3 (.out(button_3_out));
  Hex_Digit_Display hex_digit_display_3 (.value(\六十进制计数器_2_q1a ));  // open: dp
  \六十进制计数器  \u_六十进制计数器_2  (
    .Adj(in_2), .Q0d(\六十进制计数器_2_q0a [3]), .Q0c(\六十进制计数器_2_q0a [2]), .Q0b(\六十进制计数器_2_q0a [1]),
    .Q0a(\六十进制计数器_2_q0a [0]), .Q1d(\六十进制计数器_2_q1a [3]), .Q1c(\六十进制计数器_2_q1a [2]), .Q1b(\六十进制计数器_2_q1a [1]),
    .Q1a(\六十进制计数器_2_q1a [0]), .Clr(in_4), .CPU(\六十进制计数器_1_nqcc ), .CPD(button_3_out));  // open: nQcc
  Hex_Digit_Display hex_digit_display_4 (.value(\六十进制计数器_2_q0a ));  // open: dp
endmodule

module \十二进制计数器或二十四进制的计数器电路  (
  input  in_1,
  input  in_2,
  input  in_3,
  input  in_4,
  input  in_5,
  output out_6,
  output out_7,
  output out_8,
  output out_9,
  output out_10,
  output out_11,
  output out_12,
  output out_13,
  output out_14
);

  wire and_1_out, and_2_out, not_1_out, or_1_out;

  \六十进制计数器  \u_六十进制计数器_1  (
    .Adj(in_3), .Q0d(out_10), .Q0c(out_11), .Q0b(out_12), .Q0a(out_13), .Q1d(out_6), .Q1c(out_7),
    .Q1b(out_8), .Q1a(out_9), .Clr(or_1_out), .CPU(in_2), .CPD(in_4));  // open: nQcc
  not not_1 (not_1_out, in_1);
  or or_1 (or_1_out, out_14, in_5);
  and and_1 (and_1_out, out_9, out_12, not_1_out);
  and and_2 (and_2_out, out_8, out_11, in_1);
  or or_2 (out_14, and_2_out, and_1_out);
endmodule

module \十二进制计数器或二十四进制的计数器测试电路  (
  input  in_1,
  input  in_2,
  input  in_3,
  input  in_4,
  input  in_5,
  input  in_6
);

  wire button_1_out, button_2_out, button_3_out, \十二进制计数器或二十四进制的计数器电路_1_out_14 ;
  wire [3:0] \十二进制计数器或二十四进制的计数器电路_1_out_9 , \十二进制计数器或二十四进制的计数器电路_1_out_13 , \十二进制计数器或二十四进制的计数器电路_2_out_9 ,
       \十二进制计数器或二十四进制的计数器电路_2_out_13 ;

  Button button_1 (.out(button_1_out));
  Button button_2 (.out(button_2_out));
  Hex_Digit_Display hex_digit_display_1 (.value(\十二进制计数器或二十四进制的计数器电路_1_out_9 ));  // open: dp
  Hex_Digit_Display hex_digit_display_2 (.value(\十二进制计数器或二十四进制的计数器电路_1_out_13 ));  // open: dp
  \十二进制计数器或二十四进制的计数器电路  \u_十二进制计数器或二十四进制的计数器电路_1  (
    .in_3(in_1), .out_14(\十二进制计数器或二十四进制的计数器电路_1_out_14 ), .out_6(\十二进制计数器或二十四进制的计数器电路_1_out_9 [3]),
    .out_7(\十二进制计数器或二十四进制的计数器电路_1_out_9 [2]), .out_8(\十二进制计数器或二十四进制的计数器电路_1_out_9 [1]),
    .out_9(\十二进制计数器或二十四进制的计数器电路_1_out_9 [0]), .out_10(\十二进制计数器或二十四进制的计数器电路_1_out_13 [3]),
    .out_11(\十二进制计数器或二十四进制的计数器电路_1_out_13 [2]), .out_12(\十二进制计数器或二十四进制的计数器电路_1_out_13 [1]),
    .out_13(\十二进制计数器或二十四进制的计数器电路_1_out_13 [0]), .in_1(in_2), .in_2(button_1_out), .in_4(button_2_out),
    .in_5(in_5));
  Button button_3 (.out(button_3_out));
  Hex_Digit_Display hex_digit_display_3 (.value(\十二进制计数器或二十四进制的计数器电路_2_out_9 ));  // open: dp
  Hex_Digit_Display hex_digit_display_4 (.value(\十二进制计数器或二十四进制的计数器电路_2_out_13 ));  // open: dp
  \十二进制计数器或二十四进制的计数器电路  \u_十二进制计数器或二十四进制的计数器电路_2  (
    .in_3(in_3), .out_6(\十二进制计数器或二十四进制的计数器电路_2_out_9 [3]), .out_7(\十二进制计数器或二十四进制的计数器电路_2_out_9 [2]),
    .out_8(\十二进制计数器或二十四进制的计数器电路_2_out_9 [1]), .out_9(\十二进制计数器或二十四进制的计数器电路_2_out_9 [0]),
    .out_10(\十二进制计数器或二十四进制的计数器电路_2_out_13 [3]), .out_11(\十二进制计数器或二十四进制的计数器电路_2_out_13 [2]),
    .out_12(\十二进制计数器或二十四进制的计数器电路_2_out_13 [1]), .out_13(\十二进制计数器或二十四进制的计数器电路_2_out_13 [0]), .in_1(in_4),
    .in_2(\十二进制计数器或二十四进制的计数器电路_1_out_14 ), .in_4(button_3_out), .in_5(in_6));  // open: out_14
endmodule

module \上下午文字显示测试电路  (
  input  in_1,
  input  in_2
);

  wire [4:0] \上下午文字显示的电路_1_out_3 , \上下午文字显示的电路_1_out_4 , \上下午文字显示的电路_1_out_5 , \上下午文字显示的电路_1_out_6 ;

  DotMatrix #(.inputtype("column"), .matrixcols(4), .matrixrows(5), .persist(0), .dotshape("square")) dotmatrix_1 (
    .col0(\上下午文字显示的电路_1_out_3 ), .col1(\上下午文字显示的电路_1_out_4 ), .col2(\上下午文字显示的电路_1_out_5 ),
    .col3(\上下午文字显示的电路_1_out_6 ));
  \上下午文字显示的电路  \u_上下午文字显示的电路_1  (
    .in_1(in_1), .in_2(in_2), .out_3(\上下午文字显示的电路_1_out_3 ), .out_4(\上下午文字显示的电路_1_out_4 ),
    .out_5(\上下午文字显示的电路_1_out_5 ), .out_6(\上下午文字显示的电路_1_out_6 ));
endmodule

module \上下午文字显示的电路  (
  input  in_1,
  input  in_2,
  output [4:0] out_3,
  output [4:0] out_4,
  output [4:0] out_5,
  output [4:0] out_6
);

  wire not_1_out, not_2_out;

  and and_1 (out_4[4], not_1_out, in_2);
  not not_1 (not_1_out, 1'b0);
  and and_2 (out_3[0], not_2_out, in_2);
  not not_2 (not_2_out, in_1);
  and and_3 (out_3[4], in_1, in_2);

  assign out_3[3:1] = 3'b000;
  assign out_4[3:0] = {4{out_4[4]}};
  assign out_5 = {out_3[4], 1'b0, out_4[4], 1'b0, out_3[0]};
  assign out_6 = {out_3[4], 3'b000, out_3[0]};
endmodule

module \电子钟整点报时电路  (
  input  in_1,
  input  in_2,
  input  in_3,
  input  in_4,
  input  in_5,
  input  in_6,
  input  in_7,
  input  in_8,
  input  in_9,
  input  in_10,
  input  in_11,
  input  in_12,
  input  in_13,
  output out_14
);

  wire and_1_out, and_3_out, and_4_out, and_5_out, not_1_out, not_2_out, not_3_out, not_4_out, not_5_out,
       not_6_out;

  not not_1 (not_1_out, in_2);
  and and_1 (and_1_out, not_1_out, in_3, not_2_out, in_5);
  not not_2 (not_2_out, in_4);
  and and_2 (out_14, in_1, and_3_out);
  and and_3 (and_3_out, and_1_out, and_4_out, and_5_out);
  and and_4 (and_4_out, in_6, not_3_out, not_4_out, in_9);
  not not_3 (not_3_out, in_7);
  not not_4 (not_4_out, in_8);
  not not_5 (not_5_out, in_10);
  and and_5 (and_5_out, not_5_out, in_11, not_6_out, in_13);
  not not_6 (not_6_out, in_12);
endmodule

module \电子钟整点报时电路测试电路  (
  input  Adj
);

  wire Clk_out, Min_0_out, Min_minus_out, Min_plus_out, or_1_out, or_2_out, Sec_0_out, Sec_minus_out,
       Sec_plus_out, \六十进制计数器_1_nqcc , \六十进制计数器_1_q1a , \六十进制计数器_1_q1b , \六十进制计数器_1_q1c , \六十进制计数器_1_q1d ,
       \六十进制计数器_2_q0a , \六十进制计数器_2_q0b , \六十进制计数器_2_q0c , \六十进制计数器_2_q0d , \六十进制计数器_2_q1a , \六十进制计数器_2_q1b ,
       \六十进制计数器_2_q1c , \六十进制计数器_2_q1d , \电子钟整点报时电路_1_out_14 ;

  Clock #(.highDuration(1), .lowDuration(1)) Clk (.out(Clk_out));
  Button Sec_plus (.out(Sec_plus_out));
  Button Sec_minus (.out(Sec_minus_out));
  Button Min_plus (.out(Min_plus_out));
  Button Min_minus (.out(Min_minus_out));
  or or_1 (or_1_out, Sec_plus_out, Clk_out);
  \六十进制计数器  \u_六十进制计数器_1  (
    .Adj(Adj), .nQcc(\六十进制计数器_1_nqcc ), .Q1d(\六十进制计数器_1_q1d ), .Q1c(\六十进制计数器_1_q1c ), .Q1b(\六十进制计数器_1_q1b ),
    .Q1a(\六十进制计数器_1_q1a ), .Clr(Sec_0_out), .CPU(or_1_out), .CPD(Sec_minus_out));  // open: Q0d, Q0c, Q0b, Q0a
  Button Sec_0 (.out(Sec_0_out));
  or or_2 (or_2_out, \六十进制计数器_1_nqcc , Min_plus_out);
  \电子钟整点报时电路  \u_电子钟整点报时电路_1  (
    .out_14(\电子钟整点报时电路_1_out_14 ), .in_2(\六十进制计数器_2_q1d ), .in_3(\六十进制计数器_2_q1c ), .in_4(\六十进制计数器_2_q1b ),
    .in_5(\六十进制计数器_2_q1a ), .in_6(\六十进制计数器_2_q0d ), .in_1(Clk_out), .in_7(\六十进制计数器_2_q0c ),
    .in_8(\六十进制计数器_2_q0b ), .in_9(\六十进制计数器_2_q0a ), .in_10(\六十进制计数器_1_q1d ), .in_11(\六十进制计数器_1_q1c ),
    .in_12(\六十进制计数器_1_q1b ), .in_13(\六十进制计数器_1_q1a ));
  \六十进制计数器  \u_六十进制计数器_2  (
    .Adj(Adj), .Q0d(\六十进制计数器_2_q0d ), .Q0c(\六十进制计数器_2_q0c ), .Q0b(\六十进制计数器_2_q0b ), .Q0a(\六十进制计数器_2_q0a ),
    .Q1d(\六十进制计数器_2_q1d ), .Q1c(\六十进制计数器_2_q1c ), .Q1b(\六十进制计数器_2_q1b ), .Q1a(\六十进制计数器_2_q1a ),
    .Clr(Min_0_out), .CPU(or_2_out), .CPD(Min_minus_out));  // open: nQcc
  LED #(.active("true")) led_1 (.in(\电子钟整点报时电路_1_out_14 ));
  Button Min_0 (.out(Min_0_out));
endmodule

module \秒脉冲产生电路  (
  input  in_1,
  output out_2
);

  \四位二进制可逆计数器  \u_四位二进制可逆计数器_1  (
    .CPD(1'b0), .CPU(in_1), .A(1'b0), .B(1'b0), .C(1'b0), .QD(out_2), .D(1'b0), .nLD(1'b1), .CLR(out_2));  // open: QA, QB, QC
endmodule

module \闹钟  (
  input  in_1,
  input  in_2,
  input  in_3,
  input  in_4,
  input  in_5,
  input  in_6,
  input  in_7,
  input  in_8,
  input  in_9,
  input  in_10,
  input  in_11,
  input  in_12,
  input  in_13,
  input  in_14,
  input  in_15,
  input  in_16,
  input  in_17,
  input  in_18,
  input  in_19,
  input  in_20,
  input  in_21
);

  wire and_1_out, and_2_out, and_3_out, and_4_out, and_5_out, and_6_out, and_7_out, button_1_out,
       button_2_out, button_3_out, button_4_out, button_5_out, button_6_out, button_7_out, button_8_out,
       button_9_out, not_1_out, or_1_out, or_2_out, or_3_out, xnor_1_out, xnor_2_out, xnor_3_out, xnor_4_out,
       xnor_5_out, xnor_6_out, xnor_7_out, xnor_8_out, xnor_9_out, xnor_10_out, xnor_11_out, xnor_12_out,
       xnor_13_out, xnor_14_out, xnor_15_out, xnor_16_out, \六十进制计数器_1_nqcc , \六十进制计数器_2_nqcc ;
  wire [3:0] \六十进制计数器_1_q0a , \六十进制计数器_1_q1a , \六十进制计数器_2_q0a , \六十进制计数器_2_q1a ,
       \十二进制计数器或二十四进制的计数器电路_1_out_9 , \十二进制计数器或二十四进制的计数器电路_1_out_13 ;

  xnor xnor_1 (xnor_1_out, in_2, \十二进制计数器或二十四进制的计数器电路_1_out_9 [3]);
  xnor xnor_2 (xnor_2_out, in_5, \十二进制计数器或二十四进制的计数器电路_1_out_9 [2]);
  and and_1 (and_1_out, xnor_1_out, xnor_2_out, xnor_3_out, xnor_4_out);
  xnor xnor_3 (xnor_3_out, in_8, \十二进制计数器或二十四进制的计数器电路_1_out_9 [1]);
  xnor xnor_4 (xnor_4_out, in_11, \十二进制计数器或二十四进制的计数器电路_1_out_9 [0]);
  xnor xnor_5 (xnor_5_out, in_14, \十二进制计数器或二十四进制的计数器电路_1_out_13 [3]);
  and and_2 (and_2_out, and_1_out, and_3_out);
  and and_3 (and_3_out, xnor_5_out, xnor_7_out, xnor_6_out, xnor_8_out);
  xnor xnor_6 (xnor_6_out, in_18, \十二进制计数器或二十四进制的计数器电路_1_out_13 [1]);
  xnor xnor_7 (xnor_7_out, in_16, \十二进制计数器或二十四进制的计数器电路_1_out_13 [2]);
  Button button_1 (.out(button_1_out));
  xnor xnor_8 (xnor_8_out, in_20, \十二进制计数器或二十四进制的计数器电路_1_out_13 [0]);
  or or_1 (or_1_out, button_1_out, \六十进制计数器_1_nqcc );
  Button button_2 (.out(button_2_out));
  Button button_3 (.out(button_3_out));
  Hex_Digit_Display hex_digit_display_1 (.value(\十二进制计数器或二十四进制的计数器电路_1_out_9 ));  // open: dp
  Hex_Digit_Display hex_digit_display_2 (.value(\十二进制计数器或二十四进制的计数器电路_1_out_13 ));  // open: dp
  \十二进制计数器或二十四进制的计数器电路  \u_十二进制计数器或二十四进制的计数器电路_1  (
    .in_3(1'b1), .out_6(\十二进制计数器或二十四进制的计数器电路_1_out_9 [3]), .out_7(\十二进制计数器或二十四进制的计数器电路_1_out_9 [2]),
    .out_8(\十二进制计数器或二十四进制的计数器电路_1_out_9 [1]), .out_9(\十二进制计数器或二十四进制的计数器电路_1_out_9 [0]),
    .out_10(\十二进制计数器或二十四进制的计数器电路_1_out_13 [3]), .out_11(\十二进制计数器或二十四进制的计数器电路_1_out_13 [2]),
    .out_12(\十二进制计数器或二十四进制的计数器电路_1_out_13 [1]), .out_13(\十二进制计数器或二十四进制的计数器电路_1_out_13 [0]), .in_1(1'b1),
    .in_2(or_1_out), .in_4(button_2_out), .in_5(button_3_out));  // open: out_14
  xnor xnor_9 (xnor_9_out, in_6, \六十进制计数器_1_q1a [2]);
  xnor xnor_10 (xnor_10_out, in_3, \六十进制计数器_1_q1a [3]);
  and and_4 (and_4_out, xnor_10_out, xnor_9_out, xnor_11_out, xnor_12_out);
  xnor xnor_11 (xnor_11_out, in_9, \六十进制计数器_1_q1a [1]);
  xnor xnor_12 (xnor_12_out, in_12, \六十进制计数器_1_q1a [0]);
  xnor xnor_13 (xnor_13_out, in_15, \六十进制计数器_1_q0a [3]);
  and and_5 (and_5_out, and_4_out, and_6_out);
  and and_6 (and_6_out, xnor_13_out, xnor_14_out, xnor_15_out, xnor_16_out);
  xnor xnor_14 (xnor_14_out, in_17, \六十进制计数器_1_q0a [2]);
  xnor xnor_15 (xnor_15_out, in_19, \六十进制计数器_1_q0a [1]);
  Button button_4 (.out(button_4_out));
  xnor xnor_16 (xnor_16_out, in_21, \六十进制计数器_1_q0a [0]);
  \六十进制计数器  \u_六十进制计数器_1  (
    .Adj(1'b1), .Q0d(\六十进制计数器_1_q0a [3]), .Q0c(\六十进制计数器_1_q0a [2]), .Q0b(\六十进制计数器_1_q0a [1]),
    .Q0a(\六十进制计数器_1_q0a [0]), .nQcc(\六十进制计数器_1_nqcc ), .Q1d(\六十进制计数器_1_q1a [3]), .Q1c(\六十进制计数器_1_q1a [2]),
    .Q1b(\六十进制计数器_1_q1a [1]), .Q1a(\六十进制计数器_1_q1a [0]), .Clr(button_6_out), .CPU(or_2_out), .CPD(button_5_out));
  or or_2 (or_2_out, button_4_out, \六十进制计数器_2_nqcc );
  Button button_5 (.out(button_5_out));
  Button button_6 (.out(button_6_out));
  Hex_Digit_Display hex_digit_display_3 (.value(\六十进制计数器_1_q1a ));  // open: dp
  Hex_Digit_Display hex_digit_display_4 (.value(\六十进制计数器_1_q0a ));  // open: dp
  LED #(.active("true")) led_1 (.in(and_7_out));
  and and_7 (and_7_out, and_2_out, and_5_out, not_1_out, in_1);
  not not_1 (not_1_out, or_3_out);
  or or_3 (or_3_out, in_4, in_7, in_10, in_13);
  Button button_7 (.out(button_7_out));
  Hex_Digit_Display hex_digit_display_5 (.value(\六十进制计数器_2_q1a ));  // open: dp
  \六十进制计数器  \u_六十进制计数器_2  (
    .Adj(1'b1), .Q0d(\六十进制计数器_2_q0a [3]), .Q0c(\六十进制计数器_2_q0a [2]), .Q0b(\六十进制计数器_2_q0a [1]),
    .Q0a(\六十进制计数器_2_q0a [0]), .nQcc(\六十进制计数器_2_nqcc ), .Q1d(\六十进制计数器_2_q1a [3]), .Q1c(\六十进制计数器_2_q1a [2]),
    .Q1b(\六十进制计数器_2_q1a [1]), .Q1a(\六十进制计数器_2_q1a [0]), .Clr(button_9_out), .CPU(button_7_out),
    .CPD(button_8_out));
  Button button_8 (.out(button_8_out));
  Button button_9 (.out(button_9_out));
  Hex_Digit_Display hex_digit_display_6 (.value(\六十进制计数器_2_q0a ));  // open: dp
endmodule
